# Fritzing sketch Hardware_model (saved by Fritzing 0.9.4)

parts:
  Part1 = Arduino Nano 33 BLE Sense
  Head = Basic Servo
  Neck = Basic Servo
  J3 = Piezo Speaker
  Part2 = HC-SR501 Body Sensor Module
  OLED_I2C1 = OLED 128x64 I2C Monochrome Display

nets:
  GND: Part1.GND, Part1.A7, Head.gnd, Neck.gnd, J3.pin1, Part2.GND, OLED_I2C1.GND
  N1: Part1.D2, Part2.OUT
  N2: Part1.D3~, Neck.pulse
  N3: Part1.D4, Head.pulse
  N4: Part1.D5~, J3.pin2
  N5: Part1.A5, OLED_I2C1.SCK
  N6: Part1.A4, OLED_I2C1.SDA
  VCC: Part1.3V3, Head.vcc, Neck.vcc, Part2.VCC, OLED_I2C1.VDD

custom parts:
  Arduino Nano 33 BLE Sense: The Nano 33 BLE Sense (without headers) is Arduino’s 3.3V AI enabled board in the smallest available form factor: 45x18mm! The Arduino Nano 33 BLE Sense is a completely new board on a well-known form factor. It comes with a series of embedded sensors: 9 axis inertial sensor: what makes this board ideal for wearable devices humidity, and temperature sensor: to get highly accurate measurements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
  HC-SR501 Body Sensor Module: Pyroelectric Infrared PIR Motion Sensor Detector Module
